# Fritzing sketch Accel-Gyro (saved by Fritzing 0.9.3b)

parts:
  Componente1 = Arduino Uno (Rev3)
  Componente2 = InvenSense MPU6050

nets:
  N1: Componente1.A4/SDA, Componente2.SDA
  N2: Componente1.A5/SCL, Componente2.SCL
  N3: Componente1.D2, Componente2.INT
  3V3: Componente1.3V3, Componente2.VCC
  VIN: Componente1.VIN, Componente2.GND

notes:
  pin giallo provare
  Accelerometer-Gyroscope module : MPU6050
