# Fritzing sketch All together schema (saved by Fritzing 0.9.3b)

parts:
  Motor_Shield = Arduino Motor Shield (Rev3)
  Motor_1 = DC Motor
  Motor_2 = DC Motor
  Battery = LIPO-1000mAh [package=lipo-1000]
  MPU6050 = InvenSense MPU6050
  Button_On/Off = Round Pushbutton

nets:
  N1: Motor_Shield.A4, MPU6050.SDA
  N2: Motor_Shield.A5, MPU6050.SCL
  N3: Motor_Shield.D10_PWM, Button_On/Off.leg1
  GND: Motor_Shield.GND, Battery.-, MPU6050.GND, Button_On/Off.leg0
  N4: Motor_Shield.D2, MPU6050.INT
  N5: Motor_Shield.B-, Motor_1.pin_2
  N6: Motor_Shield.B+, Motor_1.pin_1
  N7: Motor_Shield.A-, Motor_2.pin_2
  N8: Motor_Shield.A+, Motor_2.pin_1
  N9: Motor_Shield.VMOT, Battery.+
  3V3: Motor_Shield.3V3, MPU6050.VCC
