# Fritzing sketch All together (saved by Fritzing 0.9.3b)

parts:
  Componente1 = Arduino Motor Shield (Rev3)
  M1 = DC Motor
  M2 = DC Motor
  U1 = LIPO-1000mAh [package=lipo-1000]
  Componente2 = InvenSense MPU6050
  S2 = Round Pushbutton

nets:
  N1: Componente1.A4, Componente2.SDA
  N2: Componente1.A5, Componente2.SCL
  N3: Componente1.D10_PWM, S2.leg1
  GND: Componente1.GND, U1.-, Componente2.GND, S2.leg0
  N4: Componente1.D2, Componente2.INT
  N5: Componente1.B-, M1.pin_2
  N6: Componente1.B+, M1.pin_1
  N7: Componente1.A-, M2.pin_2
  N8: Componente1.A+, M2.pin_1
  N9: Componente1.VMOT, U1.+
  3V3: Componente1.3V3, Componente2.VCC
